# Fritzing sketch LightSensor (saved by Fritzing 0.9.3b)
breadboards: 1

parts:
  R1 = Resistor [tolerance=±5% resistance=4.1k package=THT]
  J1 = Piezo Speaker
  R4 = Trimmer Potentiometer [maximum_resistance=10kΩ package=THT]
  R3 = Trimmer Potentiometer [maximum_resistance=10kΩ package=THT]
  R2 = Photocell (LDR) [package=THT]
  Part1 = Arduino Uno (Rev3)

nets:
  N1: R1.Pin_0, R2.pin_1, Part1.A2
  N2: R1.Pin_1, J1.pin1, Part1.GND
  N3: J1.pin2, R4.wiper
  N4: R4.leg2, Part1.A5/SCL
  N5: R3.leg1, Part1.5V
  N6: R3.wiper, R2.pin_0

// code stored in the sketch: LightSensor.ino
#define spkPin A5
#define snsPin A2
int snsVal;
int atd=50; // Ambient light test duration. Number of values collected.
int sns=25; // Sensitivity of detectecting motion.
int amUp,amLow,avg,toneVal;

void setup() {
  Serial.begin(9600);
  pinMode(spkPin,OUTPUT); // Speaker
  collectAmbient();
}

void loop() {  
  snsVal=analogRead(snsPin);
  if (snsVal >= amUp || snsVal <= amLow) {
    tone(spkPin,snsVal);
    }
  else {
    noTone(spkPin);
    }
}

void collectAmbient() {
  int i=0;
  int sum=0;
  Serial.println("Ambient light readings:");
  for (i;i<=atd;i++) {
    snsVal=analogRead(snsPin);
    sum=sum+snsVal;
  }
  Serial.print("Sum: ");
  Serial.println(sum);
  avg= sum/atd;
  Serial.print("Average: ");
  Serial.println(avg);
  amUp=avg+sns; // Upper bound of ambient light
  amLow=avg-sns; // Lower bound of ambient light
  Serial.print("Ambient average: "); 
  Serial.println(avg);
  Serial.print("Lower Ambient bound: "); 
  Serial.println(amLow);
  Serial.print("Upper Ambient bound: "); 
  Serial.println(amUp);
}
